# Fritzing sketch schematics (saved by Fritzing 0.9.5d)
breadboards: 1

parts:
  Part1 = Arduino Nano (Rev3.0)
  M1 = Dagu DGServo 9g (End View) [part_number=RS001B]
  M2 = Dagu DGServo 9g (End View) [part_number=RS001B]
  Part2 = IMU Digital Combo Board 6DOF
  S1 = Momentary Switch [package=ksa_sealed_tac_switch]
  U1 = RF-LINK_RX [package=rf-link_rx]

nets:
  GND: Part1.GND, M1.gnd, M2.gnd, Part2.GND, S1.1
  N1: Part1.D3, S1.3
  N2: Part1.D5, U1.DATA
  N3: Part1.D9, M2.pulse
  N4: Part1.D10, M1.pulse
  VCC: Part1.5V, M1.vcc, M2.vcc, Part2.3.3V
  N5: Part1.A5, Part2.SCL
  N6: Part1.A4, Part2.SDA
